// Logisim project 4 BIT DECREMENTAL.circ as structural Verilog: 1 circuit, main circuit main
module main (
  input  A3,
  input  B3,
  input  A2,
  input  B2,
  input  A1,
  input  B1,
  input  A0,
  input  B0,
  input  Cin,
  output out_10,
  output out_11,
  output out_12,
  output out_13,
  output out_14
);

  wire adder_2_cout, adder_3_cout, adder_4_cout;

  Adder #(.width(1)) adder_1 (.a(B3), .b(A3), .out(out_14), .cin(adder_2_cout), .cout(out_10));
  Adder #(.width(1)) adder_2 (.a(B2), .b(A2), .out(out_11), .cin(adder_3_cout), .cout(adder_2_cout));
  Adder #(.width(1)) adder_3 (.a(B1), .b(A1), .out(out_12), .cin(adder_4_cout), .cout(adder_3_cout));
  Adder #(.width(1)) adder_4 (.a(B0), .b(A0), .out(out_13), .cin(Cin), .cout(adder_4_cout));

  // Notes on the sheet:
  //   COUT
  //   S3
  //   S2
  //   S1
  //   S0
endmodule
