// Logisim project 4 BIT INCREMENTAL.circ as structural Verilog: 1 circuit, main circuit main
module main (
  input  A3,
  input  A2,
  input  A1,
  input  A0,
  input  B0,
  output out_6,
  output out_7,
  output out_8,
  output out_9,
  output out_10
);

  wire adder_2_cout, adder_3_cout, adder_4_cout;

  Adder #(.width(1)) adder_1 (.a(adder_2_cout), .b(A3), .out(out_10), .cout(out_6));  // open: cin
  Adder #(.width(1)) adder_2 (.a(adder_3_cout), .b(A2), .out(out_7), .cout(adder_2_cout));  // open: cin
  Adder #(.width(1)) adder_3 (.a(adder_4_cout), .b(A1), .out(out_8), .cout(adder_3_cout));  // open: cin
  Adder #(.width(1)) adder_4 (.a(B0), .b(A0), .out(out_9), .cout(adder_4_cout));  // open: cin

  // Notes on the sheet:
  //   COUT
  //   S3
  //   S2
  //   S1
  //   S0
endmodule
