// Logisim project ALU.circ as structural Verilog: 1 circuit, main circuit main
module main (
  input  in_1,
  input  [1:0] in_2,
  input  in_3,
  input  in_4,
  input  in_5,
  input  in_6,
  input  in_7,
  input  in_8,
  input  in_9,
  input  in_10,
  input  in_11,
  output out_12,
  output out_13,
  output out_14,
  output out_15,
  output out_16
);

  wire adder_1_cout, adder_2_cout, adder_3_cout, multiplexer_1_out, multiplexer_2_out, multiplexer_3_out,
       multiplexer_4_out, not_1_out, not_2_out, not_3_out, not_4_out, not_5_out;

  not not_1 (not_1_out, in_4);
  not not_2 (not_2_out, in_6);
  not not_3 (not_3_out, in_8);
  not not_4 (not_4_out, in_10);
  not not_5 (not_5_out, in_11);
  Multiplexer #(.select(2)) multiplexer_1 (
    .in0(in_4), .in1(not_1_out), .in2(in_11), .in3(not_5_out), .out(multiplexer_1_out), .sel(in_2));  // open: en
  Multiplexer #(.select(2)) multiplexer_2 (
    .in0(in_6), .in1(not_2_out), .in2(in_11), .in3(not_5_out), .out(multiplexer_2_out), .sel(in_2));  // open: en
  Multiplexer #(.select(2)) multiplexer_3 (
    .in0(in_8), .in1(not_3_out), .in2(in_11), .in3(not_5_out), .out(multiplexer_3_out), .sel(in_2));  // open: en
  Multiplexer #(.select(2)) multiplexer_4 (
    .in0(in_10), .in1(not_4_out), .in2(in_11), .in3(not_5_out), .out(multiplexer_4_out), .sel(in_2));  // open: en
  Adder #(.width(1)) adder_1 (.a(in_1), .b(multiplexer_1_out), .out(out_12), .cin(in_3), .cout(adder_1_cout));
  Adder #(.width(1)) adder_2 (.a(in_5), .b(multiplexer_2_out), .out(out_13), .cin(adder_1_cout), .cout(adder_2_cout));
  Adder #(.width(1)) adder_3 (.a(in_7), .b(multiplexer_3_out), .out(out_14), .cin(adder_2_cout), .cout(adder_3_cout));
  Adder #(.width(1)) adder_4 (.a(in_9), .b(multiplexer_4_out), .out(out_15), .cin(adder_3_cout), .cout(out_16));
endmodule
