// Logisim project CARRY LOOK AHEAD ADDER.circ as structural Verilog: 1 circuit, main circuit main
module main (
  input  A2,
  input  B2,
  input  A1,
  input  B1,
  input  in_5,
  input  B0,
  input  A3,
  input  in_8,
  input  in_9
);

  wire adder_1_out, adder_2_out, adder_3_out, adder_4_out, and_1_out, and_2_out, and_3_out, or_1_out,
       xor_1_out;

  Adder #(.width(1)) adder_1 (.a(in_8), .b(A3), .out(adder_1_out));  // open: cin, cout
  Adder #(.width(1)) adder_2 (.a(B2), .b(A2), .out(adder_2_out));  // open: cin, cout
  and and_1 (and_1_out, A1, A1);
  xor xor_1 (xor_1_out, A1, A1);
  Adder #(.width(1)) adder_3 (.a(B1), .b(A1), .out(adder_3_out), .cin(or_1_out));  // open: cout
  and and_2 (and_2_out, in_5, B0);
  and and_3 (and_3_out, xor_1_out, and_2_out);
  or or_1 (or_1_out, and_1_out, and_3_out);
  Adder #(.width(1)) adder_4 (.a(B0), .b(in_5), .out(adder_4_out), .cin(in_9));  // open: cout

  // Notes on the sheet:
  //   B3
  //   G1
  //   P1
  //   Go
  //   A0
endmodule
