// Logisim project DECODER.circ as structural Verilog: 1 circuit, main circuit main
module main (
  input  C,
  input  [1:0] A,
  output D0,
  output D1,
  output D2,
  output D3,
  output D4,
  output D5,
  output D6,
  output D7
);

  wire not_1_out;

  not not_1 (not_1_out, C);
  Decoder #(.select(2)) decoder_1 (.out0(D0), .out1(D1), .out2(D2), .out3(D3), .sel(A), .en(not_1_out));
  Decoder #(.select(2)) decoder_2 (.out0(D4), .out1(D5), .out2(D6), .out3(D7), .sel(A), .en(C));

  // Notes on the sheet:
  //   B
endmodule
