// Logisim project FULL ADDER USING TWO HALF ADDER.circ as structural Verilog: 1 circuit, main circuit main
module main (
  input  in_1,
  input  in_2,
  input  in_3
);

  wire adder_1_cout, adder_1_out, adder_2_cout, adder_2_out, or_1_out;

  Adder #(.width(1)) adder_1 (.a(in_1), .b(in_2), .out(adder_1_out), .cout(adder_1_cout));  // open: cin
  Adder #(.width(1)) adder_2 (.a(adder_1_out), .b(in_3), .out(adder_2_out), .cout(adder_2_cout));  // open: cin
  LED led_1 (.in(adder_2_out));
  or or_1 (or_1_out, adder_2_cout, adder_1_cout);
  LED led_2 (.in(or_1_out));

  // Notes on the sheet:
  //   S
endmodule
