// Logisim project FULL SUB USING HALF SUB.circ as structural Verilog: 1 circuit, main circuit main
module main (
  input  in_1,
  input  in_2,
  input  in_3
);

  wire or_1_out, subtractor_1_bout, subtractor_1_out, subtractor_2_bout, subtractor_2_out;

  Subtractor #(.width(1)) subtractor_1 (
    .a(in_1), .b(in_2), .out(subtractor_1_out), .bout(subtractor_1_bout));  // open: bin
  Subtractor #(.width(1)) subtractor_2 (
    .a(subtractor_1_out), .b(in_3), .out(subtractor_2_out), .bout(subtractor_2_bout));  // open: bin
  or or_1 (or_1_out, subtractor_2_bout, subtractor_1_bout);
  LED led_1 (.in(subtractor_2_out));
  LED led_2 (.in(or_1_out));
endmodule
