// Logisim project HALF SUBSTRACTOR.circ as structural Verilog: 1 circuit, main circuit main
module main (
  input  X,
  input  Y,
  output D,
  output Bo
);

  Subtractor #(.width(1)) subtractor_1 (.a(X), .b(Y), .out(D), .bout(Bo));  // open: bin
endmodule
