// Logisim project MUX.circ as structural Verilog: 1 circuit, main circuit main
module main (
  input  in_1,
  input  in_2,
  input  in_3,
  input  in_4,
  input  in_5,
  input  in_6,
  input  in_7
);

  wire multiplexer_1_out, multiplexer_2_out, multiplexer_3_out;

  Multiplexer multiplexer_1 (.in0(in_1), .in1(in_2), .out(multiplexer_1_out), .sel(in_3));  // open: en
  Multiplexer multiplexer_2 (.in0(in_4), .in1(in_5), .out(multiplexer_2_out), .sel(in_6));  // open: en
  Multiplexer multiplexer_3 (
    .in0(multiplexer_1_out), .in1(multiplexer_2_out), .out(multiplexer_3_out), .sel(in_7));  // open: en
  LED led_1 (.in(multiplexer_3_out));
endmodule
