// Logisim project RAM CHIP MATRIX.circ as structural Verilog: 1 circuit, main circuit main
module main (
  input  [6:0] in_1,
  input  in_2,
  input  in_3,
  input  in_4,
  input  [1:0] in_5,
  input  in_6,
  input  in_7,
  input  in_8,
  input  in_9,
  input  in_10,
  input  in_11,
  output [7:0] out_12,
  output [7:0] out_13
);

  wire decoder_1_out0, decoder_1_out1, decoder_1_out2, decoder_1_out3, undriven, undriven_2, undriven_3,
       undriven_4, undriven_5, undriven_6;

  Decoder #(.select(2)) decoder_1 (
    .out0(decoder_1_out0), .out1(decoder_1_out1), .out2(decoder_1_out2), .out3(decoder_1_out3), .sel(in_5));  // open: en
  RAM #(.addrWidth(7)) ram_1 (.addr(in_1), .data(out_12), .sel(decoder_1_out0), .ld(in_3), .clr(in_2));  // open: clk
  RAM #(.addrWidth(7)) ram_2 (
    .addr(in_1), .data(out_12), .sel(decoder_1_out1), .ld(undriven), .clr(in_2));  // open: clk
  RAM #(.addrWidth(7)) ram_3 (
    .addr(in_1), .data(out_12), .sel(decoder_1_out2), .ld(undriven_2), .clr(in_2));  // open: clk
  RAM #(.addrWidth(7)) ram_4 (
    .addr(in_1), .data(out_12), .sel(decoder_1_out3), .ld(undriven_3), .clr(in_2));  // open: clk
  RAM #(.addrWidth(7)) ram_5 (.addr(in_1), .data(out_13), .sel(decoder_1_out0), .ld(in_4), .clr(in_2));  // open: clk
  RAM #(.addrWidth(7)) ram_6 (
    .addr(in_1), .data(out_13), .sel(decoder_1_out1), .ld(undriven_4), .clr(in_2));  // open: clk
  RAM #(.addrWidth(7)) ram_7 (
    .addr(in_1), .data(out_13), .sel(decoder_1_out2), .ld(undriven_5), .clr(in_2));  // open: clk
  RAM #(.addrWidth(7)) ram_8 (
    .addr(in_1), .data(out_13), .sel(decoder_1_out3), .ld(undriven_6), .clr(in_2));  // open: clk
endmodule
